// Logisim project CPU.circ as structural Verilog
module CUPU_II (
  input  [31:0] data_in,
  input  in_2,
  input  in_3,
  output [31:0] data_out,
  output [31:0] address
);

  wire [15:0] bit_extender_1_out;
  wire [31:0] multiplexer_1_out, regs_1_data_out1, regs_1_data_out2;

  Bit_Extender #(.in_width(32), .\type ("zero")) bit_extender_1 (.in(data_in), .out(bit_extender_1_out));
  Multiplexer #(.width(32)) multiplexer_1 (.out(multiplexer_1_out));  // open: in0, in1, sel
  Multiplexer #(.select(2), .width(32)) multiplexer_2 (.out(address));  // open: in0, in1, in2, in3, sel
  Register #(.width(16)) register_1 (.D(bit_extender_1_out));  // open: en, Q, clk, clr
  control control_1 ();  // open: in_1, in_2, out_3, out_4, out_5, out_6
  regs regs_1 (
    .data_out1(regs_1_data_out1), .data_out2(regs_1_data_out2));  // open: load, target, source1, source2, data_in
  ALU alu_1 (.b(regs_1_data_out2), .a(regs_1_data_out1));  // open: op, res
endmodule

module regs (
  input  load,
  input  [2:0] target,
  input  [2:0] source1,
  input  [2:0] source2,
  input  [31:0] data_in,
  output [31:0] data_out1,
  output [31:0] data_out2
);

  wire decoder_1_out1, decoder_1_out2, decoder_1_out3, decoder_1_out4, decoder_1_out5, decoder_1_out6,
       decoder_1_out7;
  wire [31:0] register_1_q, register_2_q, register_3_q, register_4_q, register_5_q, register_6_q,
       register_7_q;

  Decoder #(.select(3)) decoder_1 (
    .out1(decoder_1_out1), .out2(decoder_1_out2), .out3(decoder_1_out3), .out4(decoder_1_out4),
    .out5(decoder_1_out5), .out6(decoder_1_out6), .out7(decoder_1_out7), .sel(target), .en(load));  // open: out0
  Register #(.width(32)) register_1 (.D(data_in), .Q(register_1_q), .clk(decoder_1_out1));  // open: en, clr
  Register #(.width(32)) register_2 (.D(data_in), .Q(register_2_q), .clk(decoder_1_out2));  // open: en, clr
  Register #(.width(32)) register_3 (.D(data_in), .Q(register_3_q), .clk(decoder_1_out3));  // open: en, clr
  Register #(.width(32)) register_4 (.D(data_in), .Q(register_4_q), .clk(decoder_1_out4));  // open: en, clr
  Register #(.width(32)) register_5 (.D(data_in), .Q(register_5_q), .clk(decoder_1_out5));  // open: en, clr
  Register #(.width(32)) register_6 (.D(data_in), .Q(register_6_q), .clk(decoder_1_out6));  // open: en, clr
  Register #(.width(32)) register_7 (.D(data_in), .Q(register_7_q), .clk(decoder_1_out7));  // open: en, clr
  Multiplexer #(.select(3), .width(32)) multiplexer_1 (
    .in0({32{1'b0}}), .in1(register_1_q), .in2(register_2_q), .in3(register_3_q), .in4(register_4_q),
    .in5(register_5_q), .in6(register_6_q), .in7(register_7_q), .out(data_out1), .sel(source1));
  Multiplexer #(.select(3), .width(32)) multiplexer_2 (
    .in0({32{1'b0}}), .in1(register_1_q), .in2(register_2_q), .in3(register_3_q), .in4(register_4_q),
    .in5(register_5_q), .in6(register_6_q), .in7(register_7_q), .out(data_out2), .sel(source2));
endmodule

module decode (
  input  [2:0] in_1,
  input  [31:0] in_2,
  input  [31:0] in_3
);

  wire [31:0] bit_extender_1_out, bit_extender_2_out, bit_extender_3_out, bit_extender_4_out;

  assign bit_extender_1_out = {{16{in_2[15]}}, in_2[15:0]};  // Bit_Extender bit_extender_1
  assign bit_extender_2_out = {{24{in_2[7]}}, in_2[7:0]};  // Bit_Extender bit_extender_2
  assign bit_extender_3_out = {{16{1'b0}}, in_2[15:0]};  // Bit_Extender bit_extender_3
  assign bit_extender_4_out = {{24{1'b0}}, in_2[7:0]};  // Bit_Extender bit_extender_4
  Multiplexer #(.select(3), .width(32)) multiplexer_1 (
    .in0(in_2), .in1(bit_extender_1_out), .in2(bit_extender_2_out), .in5(bit_extender_3_out),
    .in6(bit_extender_4_out), .out(in_3), .sel(in_1));  // open: in3, in4, in7
endmodule

module ALU (
  input  [31:0] a,
  input  [31:0] b,
  input  [4:0] op,
  output [31:0] res
);

  wire adder_1_cout, subtractor_1_bout;
  wire [4:0] bit_extender_3_out, bit_extender_4_out, bit_extender_5_out;
  wire [31:0] adder_1_out, and_1_out, bit_extender_1_out, bit_extender_2_out, divider_1_out, divider_1_rem,
       divider_2_out, divider_2_rem, fpadder_1_out, fpdivider_1_out, fpmultiplier_1_out, fpsubtractor_1_out,
       fptoint_1_p2, inttofp_1_p2, multiplier_1_cout, multiplier_1_out, multiplier_2_cout, not_1_out,
       or_1_out, shifter_1_out, shifter_2_out, subtractor_1_out, xor_1_out;

  Adder #(.width(32)) adder_1 (.a(a), .b(b), .out(adder_1_out), .cout(adder_1_cout));  // open: cin
  assign bit_extender_1_out = {{31{1'b0}}, adder_1_cout};  // Bit_Extender bit_extender_1
  Subtractor #(.width(32)) subtractor_1 (.a(a), .b(b), .out(subtractor_1_out), .bout(subtractor_1_bout));  // open: bin
  assign bit_extender_2_out = {{31{1'b0}}, subtractor_1_bout};  // Bit_Extender bit_extender_2
  Multiplier #(.mode("twosComplement"), .width(32)) multiplier_1 (
    .a(a), .b(b), .out(multiplier_1_out), .cout(multiplier_1_cout));  // open: cin
  Multiplier #(.width(32)) multiplier_2 (.a(a), .b(b), .cout(multiplier_2_cout));  // open: out, cin
  Divider #(.mode("twosComplement"), .width(32)) divider_1 (
    .a(a), .b(b), .out(divider_1_out), .rem(divider_1_rem));  // open: upper
  Divider #(.width(32)) divider_2 (.a(a), .b(b), .out(divider_2_out), .rem(divider_2_rem));  // open: upper
  FPAdder fpadder_1 (.a(a), .b(b), .out(fpadder_1_out));
  FPSubtractor fpsubtractor_1 (.a(a), .b(b), .out(fpsubtractor_1_out));
  FPMultiplier fpmultiplier_1 (.a(a), .b(b), .out(fpmultiplier_1_out));
  FPDivider fpdivider_1 (.a(a), .b(b), .out(fpdivider_1_out));
  // IntToFP #(.width(32)) inttofp_1: pin names not known; wires that end beside it: a, inttofp_1_p2
  // FPToInt #(.width(32)) fptoint_1: pin names not known; wires that end beside it: a, fptoint_1_p2
  assign or_1_out = a | b;  // OR_Gate or_1, 32 bits wide
  assign and_1_out = a & b;  // AND_Gate and_1, 32 bits wide
  assign xor_1_out = a ^ b;  // XOR_Gate xor_1, 32 bits wide
  assign not_1_out = ~a;  // NOT_Gate not_1, 32 bits wide
  Bit_Extender #(.in_width(32), .out_width(5), .\type ("zero")) bit_extender_3 (.in(b), .out(bit_extender_3_out));
  Bit_Extender #(.in_width(32), .out_width(5), .\type ("zero")) bit_extender_4 (.in(b), .out(bit_extender_4_out));
  Bit_Extender #(.in_width(32), .out_width(5), .\type ("zero")) bit_extender_5 (.in(b), .out(bit_extender_5_out));
  Shifter #(.width(32)) shifter_1 (.in(a), .\dist (bit_extender_3_out), .out(shifter_1_out));
  Shifter #(.shift("lr"), .width(32)) shifter_2 (.in(a), .\dist (bit_extender_4_out), .out(shifter_2_out));
  Shifter #(.shift("ar"), .width(32)) shifter_3 (.in(a), .\dist (bit_extender_5_out));  // open: out
  Multiplexer #(.select(5), .width(32)) multiplexer_1 (
    .in0(adder_1_out), .in1(bit_extender_1_out), .in2(subtractor_1_out), .in3(bit_extender_2_out),
    .in4(multiplier_1_out), .in5(multiplier_1_cout), .in6(multiplier_2_cout), .in7(divider_1_out),
    .in8(divider_2_out), .in9(divider_1_rem), .in10(divider_2_rem), .in11(fpadder_1_out),
    .in12(fpsubtractor_1_out), .in13(fpmultiplier_1_out), .in14(fpdivider_1_out), .in15(inttofp_1_p2),
    .in16(fptoint_1_p2), .in17(a), .in18(or_1_out), .in19(and_1_out), .in20(xor_1_out), .in21(not_1_out),
    .in22(shifter_1_out), .in23(shifter_2_out), .out(res), .sel(op));  // open: in24, in25, in26, in27, in28, in29, in30, in31
endmodule

module control (
  input  [15:0] in_1,
  input  [31:0] in_2,
  output [2:0] out_3,
  output [2:0] out_4,
  output [2:0] out_5,
  output [2:0] out_6
);

  wire and_1_out, and_2_out, decoder_1_out0, decoder_1_out1, decoder_1_out2, decoder_1_out3, decoder_2_out0,
       decoder_2_out1, decoder_2_out2, decoder_2_out3, decoder_2_out4, decoder_2_out5, decoder_2_out6,
       decoder_2_out7;

  and and_1 (and_1_out, in_1[15], in_1[14]);
  Decoder #(.select(2)) decoder_1 (
    .out0(decoder_1_out0), .out1(decoder_1_out1), .out2(decoder_1_out2), .out3(decoder_1_out3),
    .sel(in_1[10:9]), .en(and_1_out));
  Decoder #(.select(3)) decoder_2 (
    .out0(decoder_2_out0), .out1(decoder_2_out1), .out2(decoder_2_out2), .out3(decoder_2_out3),
    .out4(decoder_2_out4), .out5(decoder_2_out5), .out6(decoder_2_out6), .out7(decoder_2_out7),
    .sel(in_1[13:11]), .en(and_1_out));
  Decoder #(.select(2)) decoder_3 ();  // open: out0, out1, out2, out3, sel, en
  and and_2 (and_2_out, decoder_1_out1, decoder_2_out0);
  Multiplexer #(.width(3)) multiplexer_1 (.in0(in_1[2:0]), .in1(in_1[8:6]), .out(out_6), .sel(and_2_out));

  assign out_3 = in_1[2:0];
  assign out_4 = in_1[5:3];
  assign out_5 = in_1[8:6];
endmodule
